# Fritzing sketch Mini_Oszi (saved by Fritzing 0.9.3b)
breadboards: 1

parts:
  Part1 = Arduino Nano (Rev3.0) (ICSP)
  Nokia_5110_LCD_Module1 = Nokia5110LCDModule
  R1 = Rotary Potentiometer (Large) [maximum_resistance=22kΩ package=THT]
  R2 = Resistor [tolerance=±5% resistance=330 package="0805 [SMD]"]

nets:
  N1: Part1.D0/RX, Part1.D9, R1.leg2, R2.Pin_1
  N2: Part1.GND, Nokia_5110_LCD_Module1.Grnd, R1.leg1
  N3: Part1.D2, Part1.A0
  N4: Part1.D5, Nokia_5110_LCD_Module1.D/C
  N5: Part1.D6, Nokia_5110_LCD_Module1.RST
  N6: Part1.D7, Nokia_5110_LCD_Module1.SCE
  N7: Part1.D11/MOSI, Nokia_5110_LCD_Module1.6_DN_(MOSI)
  N8: Part1.5V, Part1.AREF
  N9: Part1.A5, R1.wiper
  3V3: Part1.3V3, Nokia_5110_LCD_Module1.Vcc
  N10: Part1.D13/SCK, Nokia_5110_LCD_Module1.SCLK
  N11: Nokia_5110_LCD_Module1.LED, R2.Pin_0

custom parts:
  : Nokia 5110 LCD with 8 pin. It's a 45mm*45mm module part. Description: The Nokia 5110 is a basic graphic LCD screen for lots of applications. It was originally intended for as a cell phone screen. This one is mounted on an easy to solder PCB. It uses the PCD8544 controller. The PCD8544 is a low power CMOS LCD controller/driver, designed to drive a graphic display of 48 rows and 84 columns. All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
